# Fritzing sketch project-fritzing (saved by Fritzing 0.9.3b)
breadboards: 1

parts:
  Part1 = Arduino Uno (Rev3)
  S1 = Pushbutton [package="[THT]"]
  S2 = Pushbutton [package="[THT]"]
  S3 = Pushbutton [package="[THT]"]
  S4 = Pushbutton [package="[THT]"]
  LED1 = LED - 5mm [color="Red (633nm)" package="5 mm [THT]"]
  R1 = Resistor [tolerance=±5% resistance=220 package=THT]
  R2 = Resistor [tolerance=±5% resistance=220 package=THT]
  R3 = Resistor [tolerance=±5% resistance=220 package=THT]
  R4 = Resistor [tolerance=±5% resistance=220 package=THT]
  R5 = Rotary Potentiometer (Small) [maximum_resistance=100kΩ package=THT]
  LED2 = LED - 5mm [color="Red (633nm)" package="5 mm [THT]"]
  LED3 = LED - 5mm [color="Red (633nm)" package="5 mm [THT]"]
  LED4 = LED - 5mm [color="Red (633nm)" package="5 mm [THT]"]

nets:
  N1: Part1.A0, R5.wiper
  N2: Part1.D4, S2.Pin_1, S2.Pin_2, LED4.anode
  N3: Part1.D5_PWM, S4.Pin_1, S4.Pin_2, LED3.anode
  N4: Part1.D6_PWM, S3.Pin_1, S3.Pin_2, LED2.anode
  N5: Part1.D7, S1.Pin_1, S1.Pin_2, LED1.anode
  N6: Part1.5V, S1.Pin_3, S1.Pin_4, S2.Pin_3, S2.Pin_4, S3.Pin_3, S3.Pin_4, S4.Pin_3, S4.Pin_4, R5.leg1
  N7: Part1.GND, R1.Pin_1, R2.Pin_1, R3.Pin_1, R4.Pin_1, R5.leg2
  N8: LED1.cathode, R1.Pin_0
  N9: R2.Pin_0, LED2.cathode
  N10: R3.Pin_0, LED3.cathode
  N11: R4.Pin_0, LED4.cathode
